// Logisim project ControlUnit.circ as structural Verilog: 2 circuits, main circuit Control Unit
module Control_Unit (
  input  [19:0] I,
  input  C,
  output DE,
  output EA,
  output FO,
  output EX,
  output SR,
  output FE
);

  wire undriven;
  wire [2:0] n3bitregister_1_out_4, undriven_2;

  _3BitRegister u_3bitregister_1 (.C(C), .E(undriven), .in_1(undriven_2), .out_4(n3bitregister_1_out_4));
  Decoder_part #(.select(3), .disabled(0), .enable("false")) decoder_1 (
    .out0(FE), .out1(DE), .out2(EA), .out3(FO), .out4(EX), .out5(SR), .sel(n3bitregister_1_out_4));  // open: out6, out7

  // Notes on the sheet:
  //   EA: pull=down
  //   I: pull=down
  //   FE: pull=down
  //   FO: pull=down
  //   DE: pull=down
  //   SR: pull=down
  //   EX: pull=down
  //   C: pull=down
endmodule

module Decoder (
  input  E,
  input  [19:0] in_2,
  output [9:0] O10,
  output [6:0] O7,
  output [2:0] ALUS,
  output IMM,
  output [2:0] NEXT,
  output [3:0] SR1,
  output [3:0] SR2,
  output [3:0] DR
);

  wire decoder_1_out1, decoder_1_out2, decoder_1_out3, decoder_1_out4, decoder_1_out5, decoder_1_out6,
       decoder_1_out7, decoder_1_out8, decoder_1_out9, decoder_1_out10, decoder_1_out11, decoder_1_out12,
       decoder_1_out13, decoder_1_out14, decoder_1_out15, decoder_1_out16, decoder_1_out17, decoder_1_out18,
       or_1_out, or_4_out, or_5_out, or_7_out, or_9_out;

  or or_1 (or_1_out, decoder_1_out3, decoder_1_out4);
  or or_2 (ALUS[0], or_1_out, or_5_out);
  or or_3 (ALUS[1], or_4_out, or_5_out);
  or or_4 (or_4_out, decoder_1_out5, decoder_1_out6);
  or or_5 (or_5_out, decoder_1_out7, decoder_1_out8);
  or or_6 (ALUS[2], decoder_1_out9, decoder_1_out10);
  Decoder_part #(.select(5), .disabled(0)) decoder_1 (
    .out1(decoder_1_out1), .out2(decoder_1_out2), .out3(decoder_1_out3), .out4(decoder_1_out4),
    .out5(decoder_1_out5), .out6(decoder_1_out6), .out7(decoder_1_out7), .out8(decoder_1_out8),
    .out9(decoder_1_out9), .out10(decoder_1_out10), .out11(decoder_1_out11), .out12(decoder_1_out12),
    .out13(decoder_1_out13), .out14(decoder_1_out14), .out15(decoder_1_out15), .out16(decoder_1_out16),
    .out17(decoder_1_out17), .out18(decoder_1_out18), .sel(in_2[19:15]), .en(E));  // open: out0, out19, out20, out21, out22, out23, out24, out25, out26, out27, out28, out29, out30, out31
  or or_7 (or_7_out, decoder_1_out9, decoder_1_out7, decoder_1_out5, decoder_1_out3, decoder_1_out1);
  or or_8 (IMM, decoder_1_out2, decoder_1_out4, decoder_1_out6, decoder_1_out8, decoder_1_out10);
  or or_9 (or_9_out, or_7_out, IMM);

  assign O7 = in_2[6:0];
  assign O10 = in_2[9:0];

  // Notes on the sheet:
  //   NEXT: pull=down
  //   ALUS: pull=down
  //   IMM: pull=down
  //   DR: pull=down
  //   O10: pull=down
  //   SR1: pull=down
  //   O7: pull=down
  //   in_2: pull=down
  //   SR2: pull=down
endmodule
