// Logisim project 20BitRegister.circ as structural Verilog: 1 circuit, main circuit 20BitRegister
module _20BitRegister (
  input  [19:0] I,
  input  C,
  output [19:0] Q
);

  RisingEdgeTriggeredDFlipFlop risingedgetriggereddflipflop_1 (.D(I[19]), .C(C), .Q(Q[19]));
  RisingEdgeTriggeredDFlipFlop risingedgetriggereddflipflop_2 (.D(I[18]), .C(C), .Q(Q[18]));
  RisingEdgeTriggeredDFlipFlop risingedgetriggereddflipflop_3 (.D(I[17]), .C(C), .Q(Q[17]));
  RisingEdgeTriggeredDFlipFlop risingedgetriggereddflipflop_4 (.D(I[16]), .C(C), .Q(Q[16]));
  RisingEdgeTriggeredDFlipFlop risingedgetriggereddflipflop_5 (.D(I[15]), .C(C), .Q(Q[15]));
  RisingEdgeTriggeredDFlipFlop risingedgetriggereddflipflop_6 (.D(I[14]), .C(C), .Q(Q[14]));
  RisingEdgeTriggeredDFlipFlop risingedgetriggereddflipflop_7 (.D(I[13]), .C(C), .Q(Q[13]));
  RisingEdgeTriggeredDFlipFlop risingedgetriggereddflipflop_8 (.D(I[12]), .C(C), .Q(Q[12]));
  RisingEdgeTriggeredDFlipFlop risingedgetriggereddflipflop_9 (.D(I[11]), .C(C), .Q(Q[11]));
  RisingEdgeTriggeredDFlipFlop risingedgetriggereddflipflop_10 (.D(I[10]), .C(C), .Q(Q[10]));
  RisingEdgeTriggeredDFlipFlop risingedgetriggereddflipflop_11 (.D(I[9]), .C(C), .Q(Q[9]));
  RisingEdgeTriggeredDFlipFlop risingedgetriggereddflipflop_12 (.D(I[8]), .C(C), .Q(Q[8]));
  RisingEdgeTriggeredDFlipFlop risingedgetriggereddflipflop_13 (.D(I[7]), .C(C), .Q(Q[7]));
  RisingEdgeTriggeredDFlipFlop risingedgetriggereddflipflop_14 (.D(I[6]), .C(C), .Q(Q[6]));
  RisingEdgeTriggeredDFlipFlop risingedgetriggereddflipflop_15 (.D(I[5]), .C(C), .Q(Q[5]));
  RisingEdgeTriggeredDFlipFlop risingedgetriggereddflipflop_16 (.D(I[4]), .C(C), .Q(Q[4]));
  RisingEdgeTriggeredDFlipFlop risingedgetriggereddflipflop_17 (.D(I[3]), .C(C), .Q(Q[3]));
  RisingEdgeTriggeredDFlipFlop risingedgetriggereddflipflop_18 (.D(I[2]), .C(C), .Q(Q[2]));
  RisingEdgeTriggeredDFlipFlop risingedgetriggereddflipflop_19 (.D(I[1]), .C(C), .Q(Q[1]));
  RisingEdgeTriggeredDFlipFlop risingedgetriggereddflipflop_20 (.D(I[0]), .C(C), .Q(Q[0]));
endmodule
